# Fritzing sketch my_garage (saved by Fritzing 0.9.3b)
breadboards: 1

parts:
  Εξάρτημα1 = Arduino Nano (Rev3.0)
  DHT2 = DHT11 Humitidy and Temperature Sensor
  R3 = Resistor [tolerance=±5% resistance=10k package=THT]

nets:
  GND: Εξάρτημα1.GND, DHT2.GND, R3.Pin_1
  N1: Εξάρτημα1.D8, DHT2.DATA, R3.Pin_0
  5V: Εξάρτημα1.5V, DHT2.VDD

custom parts:
  DHT11 Humitidy and Temperature Sensor: DHT11 Humidity and Temperature Sensor

// code stored in the sketch: nano_with_dht11.ino
#include <DHT.h>
#include <DHT_U.h>

/*####################################################################
 Kostas Tsirogiannis
 tsirogk@gmail.com
 
 I recombined two example sketches to make 
 Arduino Yun display temp and humidity to LCD (and optionally serial)
 Made from a combination of original dht11 library and the blog 
 http://www.geeetech.com/wiki/index.php/Electric_thermometer_by_using_DHT11_sensor_module
 
 BOARD -> ARDUINO YUN
 sensor www.microbot.it temp+humidity 
 * +5V   -> 5V
 * GND   -> GND
 * DATA  -> digital pin 8

 HISTORY:
 Mirko Prosseda - Original version (21/07/2013)
#######################################################################*/


//#include <LiquidCrystal.h>
#include <Adafruit_Sensor.h>
#include <DHT.h>
#include <DHT_U.h>
#define DHTTYPE           DHT11 
#define DHTPIN 8 
//LiquidCrystal lcd(12, 11, 5, 4, 3, 2);
DHT_Unified dht(DHTPIN, DHTTYPE);
void setup()

{
  Serial.begin(9600);
  Serial.println("DHT11 Humidity and Temperature Digital Sensor test sketch");
  Serial.print("LIBRARY VERSION: ");   // ??????? ?????   
Serial.println(DHT11LIB_VERSION);   
Serial.println();                    // ?????? ??????
  delay(1000);          // wait for sensor initialization
//lcd.begin(16, 2);
}

void loop()
{
Serial.print("Sensor status: ");
readTemp();

  delay(2500);
}

void readTemp(){
 // Get temperature event and print its value.
  sensors_event_t event;  
  dht.temperature().getEvent(&event);
  if (isnan(event.temperature)) {
    Serial.println("Error reading temperature!");
  }
  else {
    Serial.print("Temperature: ");
    Serial.print(event.temperature);
    Serial.println(" *C");
  }
  // Get humidity event and print its value.
  dht.humidity().getEvent(&event);
  if (isnan(event.relative_humidity)) {
    Serial.println("Error reading humidity!");
  }
  else {
    Serial.print("Humidity: ");
    Serial.print(event.relative_humidity);
    Serial.println("%");
  }
}
